# Fritzing sketch button_led (saved by Fritzing 0.9.3b)
breadboards: 1

parts:
  Raspberry_Pi_1 = Raspberry Pi 3 [part_number=RPI-3-V1.2]
  S1 = Pushbutton [package="[THT]"]
  R1 = Resistor [tolerance=±5% resistance=1k package=THT]
  R2 = Resistor [tolerance=±5% resistance=330 package=THT]
  LED1 = LED - 5mm [color="Red (633nm)" package="5 mm [THT]"]

nets:
  N1: Raspberry_Pi_1.GPIO2, S1.Pin_3, S1.Pin_4, R1.Pin_1
  N2: Raspberry_Pi_1.GIPO4, R2.Pin_1
  N3: Raspberry_Pi_1.GND, S1.Pin_1, S1.Pin_2, LED1.cathode
  N4: Raspberry_Pi_1.5V, R1.Pin_0
  N5: R2.Pin_0, LED1.anode
