# Fritzing sketch electronic_scroll (saved by Fritzing 0.9.3b)
breadboards: 1

parts:
  Raspberry_Pi_1 = Raspberry Pi 3 [part_number=RPI-3-V1.2]
  R2 = Resistor [tolerance=±5% resistance=330 package=THT]
  LED1 = LED - 5mm [color="Red (633nm)" package="5 mm [THT]"]
  SW1 = DIP Switch 8 Position [package=dipswitch-08]
  LED4 = LED - 5mm [color="Red (633nm)" package="5 mm [THT]"]
  LED3 = LED - 5mm [color="Red (633nm)" package="5 mm [THT]"]
  LED2 = LED - 5mm [color="Red (633nm)" package="5 mm [THT]"]
  R3 = Resistor [tolerance=±5% resistance=330 package=THT]
  R4 = Resistor [tolerance=±5% resistance=330 package=THT]
  R5 = Resistor [tolerance=±5% resistance=330 package=THT]

nets:
  N1: Raspberry_Pi_1.GPIO2, SW1.16
  N2: Raspberry_Pi_1.GPIO3, R2.Pin_0
  N3: Raspberry_Pi_1.GIPO4, R3.Pin_0
  N4: Raspberry_Pi_1.GND, LED1.cathode, SW1.1, LED4.cathode, LED3.cathode, LED2.cathode
  N5: Raspberry_Pi_1.GIPO17, R4.Pin_0
  N6: Raspberry_Pi_1.GIPO27, R5.Pin_0
  N7: R2.Pin_1, LED1.anode
  N8: LED4.anode, R5.Pin_1
  N9: LED3.anode, R4.Pin_1
  N10: LED2.anode, R3.Pin_1
